// Logisim project serial-adder.circ as structural Verilog: 1 circuit, main circuit main
module main (
  input  A,
  input  B,
  input  reset,
  output S,
  output Cout
);

  wire clock_out, d_ff_1_q;

  Adder #(.width(1)) adder_1 (.a(A), .b(B), .out(S), .cin(d_ff_1_q), .cout(Cout));
  Clock clock (.out(clock_out));
  D_Flip_Flop d_ff_1 (.clk(clock_out), .D(Cout), .Q(d_ff_1_q), .reset(reset));  // open: Qn, preset, en
endmodule
